# Fritzing sketch Fritzing Sketch (saved by Fritzing 0.9.3b)
breadboards: 1

parts:
  Part1 = Arduino Uno (Rev3)
  R1 = Photocell (LDR) [package=THT]
  R2 = Resistor [tolerance=±5% resistance=10k package=THT]
  R3 = Resistor [tolerance=±5% resistance=220 package=THT]
  R4 = Temperature Sensor (Thermistor) [thermistor_type=NTC package=THT]
  LED1 = LED - 5mm [color="Red (633nm)" package="5 mm [THT]"]
  LED2 = LED - 5mm [color="Red (633nm)" package="5 mm [THT]"]
  LED3 = LED - 5mm [color="Red (633nm)" package="5 mm [THT]"]
  LED4 = LED - 5mm [color="Red (633nm)" package="5 mm [THT]"]
  LED5 = LED - 5mm [color="Red (633nm)" package="5 mm [THT]"]

nets:
  N1: Part1.A0, R1.pin_1, R2.Pin_0
  N2: Part1.A1, R3.Pin_0, R4.pin_1
  N3: Part1.D13/SCK, LED1.cathode, LED2.cathode, LED3.cathode, LED4.cathode, LED5.cathode
  N4: Part1.GND, R2.Pin_1, R3.Pin_1, LED1.anode, LED2.anode, LED3.anode, LED4.anode, LED5.anode
  N5: Part1.5V, R1.pin_0, R4.pin_0
